// Logisim project CSE332_Lab6.circ as structural Verilog
module _16bit_regiister (
  input  [3:0] RS,
  input  [3:0] write_register_RD,
  input  write,
  input  [3:0] RT,
  input  [15:0] write_data,
  output [15:0] Read_data1,
  output [15:0] Read_data1_2
);

  wire and_1_out, and_2_out, and_3_out, and_4_out, and_5_out, and_6_out, and_7_out, and_8_out, and_9_out,
       and_10_out, and_11_out, and_12_out, and_13_out, and_14_out, and_15_out, and_16_out, CLK_out,
       decoder_1_out0, decoder_1_out1, decoder_1_out2, decoder_1_out3, decoder_1_out4, decoder_1_out5,
       decoder_1_out6, decoder_1_out7, decoder_1_out8, decoder_1_out9, decoder_1_out10, decoder_1_out11,
       decoder_1_out12, decoder_1_out13, decoder_1_out14, decoder_1_out15;
  wire [15:0] _0_q, _1_q, _2_q, _3_q, _4_q, _5_q, _6_q, _7_q, _8_q, _9_q, _10_q, _11_q, _12_q, _13_q, _14_q,
       _15_q;

  Decoder #(.select(4)) decoder_1 (
    .out0(decoder_1_out0), .out1(decoder_1_out1), .out2(decoder_1_out2), .out3(decoder_1_out3),
    .out4(decoder_1_out4), .out5(decoder_1_out5), .out6(decoder_1_out6), .out7(decoder_1_out7),
    .out8(decoder_1_out8), .out9(decoder_1_out9), .out10(decoder_1_out10), .out11(decoder_1_out11),
    .out12(decoder_1_out12), .out13(decoder_1_out13), .out14(decoder_1_out14), .out15(decoder_1_out15),
    .sel(write_register_RD));  // open: en
  Clock CLK (.out(CLK_out));
  and and_1 (and_1_out, write, decoder_1_out0);
  and and_2 (and_2_out, write, decoder_1_out1);
  and and_3 (and_3_out, write, decoder_1_out2);
  and and_4 (and_4_out, write, decoder_1_out3);
  and and_5 (and_5_out, write, decoder_1_out4);
  and and_6 (and_6_out, write, decoder_1_out5);
  and and_7 (and_7_out, write, decoder_1_out6);
  and and_8 (and_8_out, write, decoder_1_out7);
  and and_9 (and_9_out, write, decoder_1_out8);
  and and_10 (and_10_out, write, decoder_1_out9);
  and and_11 (and_11_out, write, decoder_1_out10);
  and and_12 (and_12_out, write, decoder_1_out11);
  and and_13 (and_13_out, write, decoder_1_out12);
  and and_14 (and_14_out, write, decoder_1_out13);
  and and_15 (and_15_out, write, decoder_1_out14);
  and and_16 (and_16_out, write, decoder_1_out15);
  Register #(.width(16)) _0 (.D(write_data), .en(and_1_out), .Q(_0_q), .clk(CLK_out));  // open: clr
  Register #(.width(16)) _1 (.D(write_data), .en(and_2_out), .Q(_1_q), .clk(CLK_out));  // open: clr
  Register #(.width(16)) _2 (.D(write_data), .en(and_3_out), .Q(_2_q), .clk(CLK_out));  // open: clr
  Register #(.width(16)) _3 (.D(write_data), .en(and_4_out), .Q(_3_q), .clk(CLK_out));  // open: clr
  Register #(.width(16)) _4 (.D(write_data), .en(and_5_out), .Q(_4_q), .clk(CLK_out));  // open: clr
  Register #(.width(16)) _5 (.D(write_data), .en(and_6_out), .Q(_5_q), .clk(CLK_out));  // open: clr
  Register #(.width(16)) _6 (.D(write_data), .en(and_7_out), .Q(_6_q), .clk(CLK_out));  // open: clr
  Register #(.width(16)) _7 (.D(write_data), .en(and_8_out), .Q(_7_q), .clk(CLK_out));  // open: clr
  Register #(.width(16)) _8 (.D(write_data), .en(and_9_out), .Q(_8_q), .clk(CLK_out));  // open: clr
  Register #(.width(16)) _9 (.D(write_data), .en(and_10_out), .Q(_9_q), .clk(CLK_out));  // open: clr
  Register #(.width(16)) _10 (.D(write_data), .en(and_11_out), .Q(_10_q), .clk(CLK_out));  // open: clr
  Register #(.width(16)) _11 (.D(write_data), .en(and_12_out), .Q(_11_q), .clk(CLK_out));  // open: clr
  Register #(.width(16)) _12 (.D(write_data), .en(and_13_out), .Q(_12_q), .clk(CLK_out));  // open: clr
  Register #(.width(16)) _13 (.D(write_data), .en(and_14_out), .Q(_13_q), .clk(CLK_out));  // open: clr
  Register #(.width(16)) _14 (.D(write_data), .en(and_15_out), .Q(_14_q), .clk(CLK_out));  // open: clr
  Register #(.width(16)) _15 (.D(write_data), .en(and_16_out), .Q(_15_q), .clk(CLK_out));  // open: clr
  Multiplexer #(.select(4), .width(16)) multiplexer_1 (
    .in0(_0_q), .in1(_1_q), .in2(_2_q), .in3(_3_q), .in4(_4_q), .in5(_5_q), .in6(_6_q), .in7(_7_q),
    .in8(_8_q), .in9(_9_q), .in10(_10_q), .in11(_11_q), .in12(_12_q), .in13(_13_q), .in14(_14_q),
    .in15(_15_q), .out(Read_data1), .sel(RS));  // open: en
  Multiplexer #(.select(4), .width(16)) multiplexer_2 (
    .in0(_0_q), .in1(_1_q), .in2(_2_q), .in3(_3_q), .in4(_4_q), .in5(_5_q), .in6(_6_q), .in7(_7_q),
    .in8(_8_q), .in9(_9_q), .in10(_10_q), .in11(_11_q), .in12(_12_q), .in13(_13_q), .in14(_14_q),
    .in15(_15_q), .out(Read_data1_2), .sel(RT));  // open: en

  // Notes on the sheet:
  //   Mahbub Ahmed Turza; ID:2211063042
endmodule

module _1bit_alu (
  input  B,
  input  A,
  input  Cin,
  input  [1:0] operaton,
  input  add_sub,
  output Output,
  output Cout
);

  wire adder_1_out, and_1_out, multiplexer_1_out, not_1_out, or_1_out;

  not not_1 (not_1_out, B);
  Multiplexer multiplexer_1 (.in0(not_1_out), .in1(B), .out(multiplexer_1_out), .sel(add_sub));  // open: en
  and and_1 (and_1_out, A, multiplexer_1_out);
  or or_1 (or_1_out, A, multiplexer_1_out);
  Adder #(.width(1)) adder_1 (.a(A), .b(multiplexer_1_out), .out(adder_1_out), .cin(Cin), .cout(Cout));
  Multiplexer #(.select(2)) multiplexer_2 (
    .in0(and_1_out), .in1(or_1_out), .in2(adder_1_out), .in3(adder_1_out), .out(Output), .sel(operaton));  // open: en

  // Notes on the sheet:
  //   Mahbub Ahmed Turza; ID:2211063042
endmodule

module _16bit_ALU (
  input  [15:0] A,
  input  [15:0] B,
  input  Cin,
  input  ADD_SUB,
  input  [1:0] operation,
  output [15:0] Output,
  output Cout
);

  wire n1bit_alu_1_cout, n1bit_alu_2_cout, n1bit_alu_3_cout, n1bit_alu_4_cout, n1bit_alu_5_cout,
       n1bit_alu_6_cout, n1bit_alu_7_cout, n1bit_alu_8_cout, n1bit_alu_9_cout, n1bit_alu_10_cout,
       n1bit_alu_11_cout, n1bit_alu_12_cout, n1bit_alu_13_cout, n1bit_alu_14_cout, n1bit_alu_15_cout;

  _1bit_alu u_1bit_alu_1 (
    .B(B[0]), .A(A[0]), .Cin(Cin), .add_sub(ADD_SUB), .Cout(n1bit_alu_1_cout), .operaton(operation),
    .Output(Output[0]));
  _1bit_alu u_1bit_alu_2 (
    .B(B[1]), .A(A[1]), .Cin(n1bit_alu_1_cout), .add_sub(ADD_SUB), .Cout(n1bit_alu_2_cout),
    .operaton(operation), .Output(Output[1]));
  _1bit_alu u_1bit_alu_3 (
    .B(B[2]), .A(A[2]), .Cin(n1bit_alu_2_cout), .add_sub(ADD_SUB), .Cout(n1bit_alu_3_cout),
    .operaton(operation), .Output(Output[2]));
  _1bit_alu u_1bit_alu_4 (
    .B(B[3]), .A(A[3]), .Cin(n1bit_alu_3_cout), .add_sub(ADD_SUB), .Cout(n1bit_alu_4_cout),
    .operaton(operation), .Output(Output[3]));
  _1bit_alu u_1bit_alu_5 (
    .B(B[4]), .A(A[4]), .Cin(n1bit_alu_4_cout), .add_sub(ADD_SUB), .Cout(n1bit_alu_5_cout),
    .operaton(operation), .Output(Output[4]));
  _1bit_alu u_1bit_alu_6 (
    .B(B[5]), .A(A[5]), .Cin(n1bit_alu_5_cout), .add_sub(ADD_SUB), .Cout(n1bit_alu_6_cout),
    .operaton(operation), .Output(Output[5]));
  _1bit_alu u_1bit_alu_7 (
    .B(B[6]), .A(A[6]), .Cin(n1bit_alu_6_cout), .add_sub(ADD_SUB), .Cout(n1bit_alu_7_cout),
    .operaton(operation), .Output(Output[6]));
  _1bit_alu u_1bit_alu_8 (
    .B(B[7]), .A(A[7]), .Cin(n1bit_alu_7_cout), .add_sub(ADD_SUB), .Cout(n1bit_alu_8_cout),
    .operaton(operation), .Output(Output[7]));
  _1bit_alu u_1bit_alu_9 (
    .B(B[8]), .A(A[8]), .Cin(n1bit_alu_8_cout), .add_sub(ADD_SUB), .Cout(n1bit_alu_9_cout),
    .operaton(operation), .Output(Output[8]));
  _1bit_alu u_1bit_alu_10 (
    .B(B[9]), .A(A[9]), .Cin(n1bit_alu_9_cout), .add_sub(ADD_SUB), .Cout(n1bit_alu_10_cout),
    .operaton(operation), .Output(Output[9]));
  _1bit_alu u_1bit_alu_11 (
    .B(B[10]), .A(A[10]), .Cin(n1bit_alu_10_cout), .add_sub(ADD_SUB), .Cout(n1bit_alu_11_cout),
    .operaton(operation), .Output(Output[10]));
  _1bit_alu u_1bit_alu_12 (
    .B(B[11]), .A(A[11]), .Cin(n1bit_alu_11_cout), .add_sub(ADD_SUB), .Cout(n1bit_alu_12_cout),
    .operaton(operation), .Output(Output[11]));
  _1bit_alu u_1bit_alu_13 (
    .B(B[12]), .A(A[12]), .Cin(n1bit_alu_12_cout), .add_sub(ADD_SUB), .Cout(n1bit_alu_13_cout),
    .operaton(operation), .Output(Output[12]));
  _1bit_alu u_1bit_alu_14 (
    .B(B[13]), .A(A[13]), .Cin(n1bit_alu_13_cout), .add_sub(ADD_SUB), .Cout(n1bit_alu_14_cout),
    .operaton(operation), .Output(Output[13]));
  _1bit_alu u_1bit_alu_15 (
    .B(B[14]), .A(A[14]), .Cin(n1bit_alu_14_cout), .add_sub(ADD_SUB), .Cout(n1bit_alu_15_cout),
    .operaton(operation), .Output(Output[14]));
  _1bit_alu u_1bit_alu_16 (
    .B(B[15]), .A(A[15]), .Cin(n1bit_alu_15_cout), .add_sub(ADD_SUB), .Cout(Cout), .operaton(operation),
    .Output(Output[15]));

  // Notes on the sheet:
  //   Mahbub Ahmed Turza; ID:2211063042
endmodule
