// Logisim project Datapath Deign.circ as structural Verilog: 7 circuits, main circuit main
module main (
  input  CIN,
  input  [3:0] in_2,
  input  [3:0] in_3,
  input  [3:0] in_4,
  input  [15:0] WRITEDATA,
  input  [1:0] SELECT,
  input  WRITE_CONTROL,
  output [15:0] SUM,
  output [15:0] READ1,
  output ZEROFLAG,
  output OVERFLOW,
  output [15:0] READ2,
  output COUT
);

  wire n16_bit_register_1_p6;

  // _16_Bit_Register 16_bit_register_1: pin names not known; wires that end beside it: in_2, in_3, in_4, WRITEDATA, WRITE_CONTROL, n16_bit_register_1_p6, READ1, READ2
  Clock CLOCK (.out(n16_bit_register_1_p6));
  _16_Bit_ALU u_16_bit_alu_1 (
    .CIN(CIN), .A(READ1), .B(READ2), .S(SELECT), .SUM(SUM), .ZEROFLAG(ZEROFLAG), .OVERFLOW(OVERFLOW),
    .COUT(COUT));

  // Notes on the sheet:
  //   REGISERFLIE
endmodule

module _16_Bit_Register (
  input  [3:0] READREGISTER1,
  input  [3:0] WRITEREGISTER,
  input  [3:0] READREGISTER2,
  input  [15:0] WRITEDATA,
  input  WRITECONTROL,
  input  CONTROL,
  output [15:0] READDATA1,
  output [15:0] READDATA2
);

  wire and_1_out, and_2_out, and_3_out, and_4_out, and_5_out, and_6_out, and_7_out, and_8_out, and_9_out,
       and_10_out, and_11_out, and_12_out, and_13_out, and_14_out, and_15_out, and_16_out, decoder_1_out0,
       decoder_1_out1, decoder_1_out2, decoder_1_out3, decoder_1_out4, decoder_1_out5, decoder_1_out6,
       decoder_1_out7, decoder_1_out8, decoder_1_out9, decoder_1_out10, decoder_1_out11, decoder_1_out12,
       decoder_1_out13, decoder_1_out14, decoder_1_out15;
  wire [15:0] register_1_q, register_2_q, register_3_q, register_4_q, register_5_q, register_6_q,
       register_7_q, register_8_q, register_9_q, register_10_q, register_11_q, register_12_q, register_13_q,
       register_14_q, register_15_q, register_16_q;

  Decoder #(.select(4)) decoder_1 (
    .out0(decoder_1_out0), .out1(decoder_1_out1), .out2(decoder_1_out2), .out3(decoder_1_out3),
    .out4(decoder_1_out4), .out5(decoder_1_out5), .out6(decoder_1_out6), .out7(decoder_1_out7),
    .out8(decoder_1_out8), .out9(decoder_1_out9), .out10(decoder_1_out10), .out11(decoder_1_out11),
    .out12(decoder_1_out12), .out13(decoder_1_out13), .out14(decoder_1_out14), .out15(decoder_1_out15),
    .sel(WRITEREGISTER));  // open: en
  and and_1 (and_1_out, decoder_1_out0, WRITECONTROL);
  and and_2 (and_2_out, decoder_1_out1, WRITECONTROL);
  and and_3 (and_3_out, decoder_1_out2, WRITECONTROL);
  and and_4 (and_4_out, decoder_1_out3, WRITECONTROL);
  and and_5 (and_5_out, decoder_1_out4, WRITECONTROL);
  and and_6 (and_6_out, decoder_1_out5, WRITECONTROL);
  and and_7 (and_7_out, decoder_1_out6, WRITECONTROL);
  and and_8 (and_8_out, decoder_1_out7, WRITECONTROL);
  and and_9 (and_9_out, decoder_1_out8, WRITECONTROL);
  and and_10 (and_10_out, decoder_1_out9, WRITECONTROL);
  and and_11 (and_11_out, decoder_1_out10, WRITECONTROL);
  and and_12 (and_12_out, decoder_1_out11, WRITECONTROL);
  and and_13 (and_13_out, decoder_1_out12, WRITECONTROL);
  and and_14 (and_14_out, decoder_1_out13, WRITECONTROL);
  and and_15 (and_15_out, decoder_1_out14, WRITECONTROL);
  and and_16 (and_16_out, decoder_1_out15, WRITECONTROL);
  Register #(.width(16)) register_1 (.D(WRITEDATA), .en(and_1_out), .Q(register_1_q), .clk(CONTROL));  // open: clr
  Register #(.width(16)) register_2 (.D(WRITEDATA), .en(and_2_out), .Q(register_2_q), .clk(CONTROL));  // open: clr
  Register #(.width(16)) register_3 (.D(WRITEDATA), .en(and_3_out), .Q(register_3_q), .clk(CONTROL));  // open: clr
  Register #(.width(16)) register_4 (.D(WRITEDATA), .en(and_4_out), .Q(register_4_q), .clk(CONTROL));  // open: clr
  Register #(.width(16)) register_5 (.D(WRITEDATA), .en(and_5_out), .Q(register_5_q), .clk(CONTROL));  // open: clr
  Register #(.width(16)) register_6 (.D(WRITEDATA), .en(and_6_out), .Q(register_6_q), .clk(CONTROL));  // open: clr
  Register #(.width(16)) register_7 (.D(WRITEDATA), .en(and_7_out), .Q(register_7_q), .clk(CONTROL));  // open: clr
  Register #(.width(16)) register_8 (.D(WRITEDATA), .en(and_8_out), .Q(register_8_q), .clk(CONTROL));  // open: clr
  Register #(.width(16)) register_9 (.D(WRITEDATA), .en(and_9_out), .Q(register_9_q), .clk(CONTROL));  // open: clr
  Register #(.width(16)) register_10 (.D(WRITEDATA), .en(and_10_out), .Q(register_10_q), .clk(CONTROL));  // open: clr
  Register #(.width(16)) register_11 (.D(WRITEDATA), .en(and_11_out), .Q(register_11_q), .clk(CONTROL));  // open: clr
  Register #(.width(16)) register_12 (.D(WRITEDATA), .en(and_12_out), .Q(register_12_q), .clk(CONTROL));  // open: clr
  Register #(.width(16)) register_13 (.D(WRITEDATA), .en(and_13_out), .Q(register_13_q), .clk(CONTROL));  // open: clr
  Register #(.width(16)) register_14 (.D(WRITEDATA), .en(and_14_out), .Q(register_14_q), .clk(CONTROL));  // open: clr
  Register #(.width(16)) register_15 (.D(WRITEDATA), .en(and_15_out), .Q(register_15_q), .clk(CONTROL));  // open: clr
  Register #(.width(16)) register_16 (.D(WRITEDATA), .en(and_16_out), .Q(register_16_q), .clk(CONTROL));  // open: clr
  Multiplexer #(.select(4), .width(16)) multiplexer_1 (
    .in0(register_1_q), .in1(register_2_q), .in2(register_3_q), .in3(register_4_q), .in4(register_5_q),
    .in5(register_6_q), .in6(register_7_q), .in7(register_8_q), .in8(register_9_q), .in9(register_10_q),
    .in10(register_11_q), .in11(register_12_q), .in12(register_13_q), .in13(register_14_q),
    .in14(register_15_q), .in15(register_16_q), .out(READDATA1), .sel(READREGISTER1));  // open: en
  Multiplexer #(.select(4), .width(16)) multiplexer_2 (
    .in0(register_1_q), .in1(register_2_q), .in2(register_3_q), .in3(register_4_q), .in4(register_5_q),
    .in5(register_6_q), .in6(register_7_q), .in7(register_8_q), .in8(register_9_q), .in9(register_10_q),
    .in10(register_11_q), .in11(register_12_q), .in12(register_13_q), .in13(register_14_q),
    .in14(register_15_q), .in15(register_16_q), .out(READDATA2), .sel(READREGISTER2));  // open: en
endmodule

module _1_Bit_ALU (
  input  A,
  input  CIN,
  input  B,
  input  [1:0] SELECT,
  output SUM,
  output COUT
);

  wire adder_1_out, and_1_out, and_2_out, multiplexer_1_out, not_1_out, or_1_out;

  and and_1 (and_1_out, A, B);
  or or_1 (or_1_out, A, B);
  not not_1 (not_1_out, B);
  Multiplexer multiplexer_1 (.in0(A), .in1(not_1_out), .out(multiplexer_1_out), .sel(and_2_out));  // open: en
  and and_2 (and_2_out, CIN, CIN, CIN);
  Adder #(.width(1)) adder_1 (.a(A), .b(multiplexer_1_out), .out(adder_1_out), .cin(CIN), .cout(COUT));
  Multiplexer #(.select(2)) multiplexer_2 (
    .in0(and_1_out), .in1(or_1_out), .in2(adder_1_out), .in3(adder_1_out), .out(SUM), .sel({2{CIN}}));  // open: en

  assign SELECT = {2{CIN}};
endmodule

module _16_Bit_ALU (
  input  CIN,
  input  [15:0] A,
  input  [15:0] B,
  input  [1:0] S,
  output [15:0] SUM,
  output ZEROFLAG,
  output OVERFLOW,
  output COUT
);

  wire n1_bit_alu_1_cout, n1_bit_alu_2_cout, n1_bit_alu_3_cout, n1_bit_alu_4_cout, n1_bit_alu_5_cout,
       n1_bit_alu_6_cout, n1_bit_alu_7_cout, n1_bit_alu_8_cout, n1_bit_alu_9_cout, n1_bit_alu_10_cout,
       n1_bit_alu_11_cout, n1_bit_alu_12_cout, n1_bit_alu_13_cout, n1_bit_alu_14_cout, n1_bit_alu_15_cout;

  _1_Bit_ALU u_1_bit_alu_1 (.A(A[0]), .CIN(CIN), .B(B[0]), .SELECT(S), .SUM(SUM[0]), .COUT(n1_bit_alu_1_cout));
  _1_Bit_ALU u_1_bit_alu_2 (
    .A(A[1]), .CIN(n1_bit_alu_1_cout), .B(B[1]), .SUM(SUM[1]), .COUT(n1_bit_alu_2_cout));  // open: SELECT
  _1_Bit_ALU u_1_bit_alu_3 (
    .A(A[2]), .CIN(n1_bit_alu_2_cout), .B(B[2]), .SUM(SUM[2]), .COUT(n1_bit_alu_3_cout));  // open: SELECT
  _1_Bit_ALU u_1_bit_alu_4 (
    .A(A[3]), .CIN(n1_bit_alu_3_cout), .B(B[3]), .SUM(SUM[3]), .COUT(n1_bit_alu_4_cout));  // open: SELECT
  _1_Bit_ALU u_1_bit_alu_5 (
    .A(A[4]), .CIN(n1_bit_alu_4_cout), .B(B[4]), .SUM(SUM[4]), .COUT(n1_bit_alu_5_cout));  // open: SELECT
  _1_Bit_ALU u_1_bit_alu_6 (
    .A(A[5]), .CIN(n1_bit_alu_5_cout), .B(B[5]), .SUM(SUM[5]), .COUT(n1_bit_alu_6_cout));  // open: SELECT
  _1_Bit_ALU u_1_bit_alu_7 (
    .A(A[6]), .CIN(n1_bit_alu_6_cout), .B(B[6]), .SUM(SUM[6]), .COUT(n1_bit_alu_7_cout));  // open: SELECT
  _1_Bit_ALU u_1_bit_alu_8 (
    .A(A[7]), .CIN(n1_bit_alu_7_cout), .B(B[7]), .SUM(SUM[7]), .COUT(n1_bit_alu_8_cout));  // open: SELECT
  _1_Bit_ALU u_1_bit_alu_9 (
    .A(A[8]), .CIN(n1_bit_alu_8_cout), .B(B[8]), .SUM(SUM[8]), .COUT(n1_bit_alu_9_cout));  // open: SELECT
  _1_Bit_ALU u_1_bit_alu_10 (
    .A(A[9]), .CIN(n1_bit_alu_9_cout), .B(B[9]), .SUM(SUM[9]), .COUT(n1_bit_alu_10_cout));  // open: SELECT
  _1_Bit_ALU u_1_bit_alu_11 (
    .A(A[10]), .CIN(n1_bit_alu_10_cout), .B(B[10]), .SUM(SUM[10]), .COUT(n1_bit_alu_11_cout));  // open: SELECT
  _1_Bit_ALU u_1_bit_alu_12 (
    .A(A[11]), .CIN(n1_bit_alu_11_cout), .B(B[11]), .SUM(SUM[11]), .COUT(n1_bit_alu_12_cout));  // open: SELECT
  _1_Bit_ALU u_1_bit_alu_13 (
    .A(A[12]), .CIN(n1_bit_alu_12_cout), .B(B[12]), .SUM(SUM[12]), .COUT(n1_bit_alu_13_cout));  // open: SELECT
  _1_Bit_ALU u_1_bit_alu_14 (
    .A(A[13]), .CIN(n1_bit_alu_13_cout), .B(B[13]), .SUM(SUM[13]), .COUT(n1_bit_alu_14_cout));  // open: SELECT
  _1_Bit_ALU u_1_bit_alu_15 (
    .A(A[14]), .CIN(n1_bit_alu_14_cout), .B(B[14]), .SUM(SUM[14]), .COUT(n1_bit_alu_15_cout));  // open: SELECT
  _1_Bit_ALU u_1_bit_alu_16 (
    .A(A[15]), .CIN(n1_bit_alu_15_cout), .B(B[15]), .SUM(SUM[15]), .COUT(COUT));  // open: SELECT
  xor xor_1 (OVERFLOW, n1_bit_alu_15_cout, COUT);
  nor nor_1 (ZEROFLAG, SUM[0], SUM[1], SUM[2], SUM[3], SUM[4], SUM[5], SUM[6], SUM[7], SUM[8], SUM[9], SUM[10], SUM[11], SUM[12], SUM[13], SUM[14], SUM[15]);
endmodule

module rpath (
  input  in_1,
  input  in_2,
  input  in_3,
  input  in_4,
  output out_5,
  output out_6,
  output out_7
);

  wire [1:0] adder_1_out, bit_extender_1_out, register_1_q;
  wire [15:0] n16_bit_alu_1_sum, n16_bit_register_1_readdata1, n16_bit_register_1_readdata2, rom_1_data;

  Register #(.width(2)) register_1 (.D(adder_1_out), .Q(register_1_q), .clk(in_2), .clr(in_4));  // open: en
  Adder #(.width(2)) adder_1 (.a(2'b01), .b(register_1_q), .out(adder_1_out));  // open: cin, cout
  ROM #(.addrWidth(2), .dataWidth(16)) rom_1 (.addr(register_1_q), .data(rom_1_data));  // open: sel
  _16_Bit_Register u_16_bit_register_1 (
    .WRITEREGISTER(rom_1_data[11:8]), .WRITEDATA(n16_bit_alu_1_sum),
    .READDATA1(n16_bit_register_1_readdata1), .READREGISTER1(rom_1_data[3:0]),
    .READDATA2(n16_bit_register_1_readdata2), .READREGISTER2(rom_1_data[7:4]), .WRITECONTROL(in_2),
    .CONTROL(in_3));
  Bit_Extender #(.in_width(4), .out_width(2)) bit_extender_1 (.in(rom_1_data[15:12]), .out(bit_extender_1_out));
  _16_Bit_ALU u_16_bit_alu_1 (
    .CIN(in_1), .A(n16_bit_register_1_readdata1), .B(n16_bit_register_1_readdata2), .S(bit_extender_1_out),
    .SUM(n16_bit_alu_1_sum), .ZEROFLAG(out_5), .OVERFLOW(out_6), .COUT(out_7));

  // Notes on the sheet:
  //   contents of rom_1 (hex, n*v repeats v):
  //   325
endmodule

module ipath (
  input  in_1,
  input  in_2,
  input  in_3,
  input  in_4,
  input  in_5,
  input  in_6,
  output out_7,
  output out_8,
  output out_9
);

  wire clock_1_out;
  wire [1:0] bit_extender_2_out;
  wire [15:0] adder_1_out, bit_extender_1_out, n16_bit_alu_1_sum, n16_bit_register_1_readdata1,
       n16_bit_register_1_readdata2, ram_1_data, register_1_q, rom_1_data;

  Clock clock_1 (.out(clock_1_out));
  Register #(.width(16)) register_1 (.D(adder_1_out), .Q(register_1_q), .clk(clock_1_out), .clr(in_4));  // open: en
  Adder #(.width(16)) adder_1 (.a(16'h1), .b(register_1_q), .out(adder_1_out));  // open: cin, cout
  ROM #(.addrWidth(16), .dataWidth(16)) rom_1 (.addr(register_1_q), .data(rom_1_data));  // open: sel
  assign bit_extender_1_out = {{12{1'b0}}, rom_1_data[3:0]};  // Bit_Extender bit_extender_1
  _16_Bit_Register u_16_bit_register_1 (
    .WRITEREGISTER(rom_1_data[7:4]), .WRITEDATA(ram_1_data), .READDATA1(n16_bit_register_1_readdata1),
    .READREGISTER1(rom_1_data[11:8]), .READDATA2(n16_bit_register_1_readdata2),
    .READREGISTER2(rom_1_data[7:4]), .WRITECONTROL(clock_1_out), .CONTROL(in_2));
  Bit_Extender #(.in_width(4), .out_width(2)) bit_extender_2 (.in(rom_1_data[15:12]), .out(bit_extender_2_out));
  _16_Bit_ALU u_16_bit_alu_1 (
    .CIN(in_1), .A(n16_bit_register_1_readdata1), .B(bit_extender_1_out), .S(bit_extender_2_out),
    .SUM(n16_bit_alu_1_sum), .ZEROFLAG(out_7), .OVERFLOW(out_8), .COUT(out_9));
  RAM #(.addrWidth(16), .dataWidth(16), .bus("separate")) ram_1 (
    .addr(n16_bit_alu_1_sum), .din(n16_bit_register_1_readdata2), .data(ram_1_data), .str(in_3), .sel(in_5),
    .clk(clock_1_out), .ld(in_6));  // open: clr

  // Notes on the sheet:
  //   Faisal Mahmud Abir 2132358642
endmodule

module Combined_datapath (
  input  in_1,
  input  in_2,
  input  in_3,
  input  in_4,
  input  in_5,
  input  in_6,
  input  in_7,
  input  in_8,
  input  in_9,
  output out_10,
  output out_11,
  output out_12
);

  wire clock_1_out;
  wire [1:0] bit_extender_2_out;
  wire [3:0] multiplexer_1_out, rom_1_data_2;
  wire [15:0] adder_1_out, bit_extender_1_out, multiplexer_2_out, multiplexer_3_out, n16_bit_alu_1_sum,
       n16_bit_register_1_readdata1, n16_bit_register_1_readdata2, ram_1_data, register_1_q, rom_1_data;

  Clock clock_1 (.out(clock_1_out));
  Register #(.width(16)) register_1 (.D(adder_1_out), .Q(register_1_q), .clk(clock_1_out), .clr(in_4));  // open: en
  Adder #(.width(16)) adder_1 (.a(16'h1), .b(register_1_q), .out(adder_1_out));  // open: cin, cout
  ROM #(.addrWidth(16), .dataWidth(16)) rom_1 (
    .addr(register_1_q), .data({rom_1_data[15:12], rom_1_data_2, rom_1_data[7:0]}));  // open: sel
  Multiplexer #(.width(4)) multiplexer_1 (
    .in0(rom_1_data[3:0]), .in1(rom_1_data_2), .out(multiplexer_1_out), .sel(in_9));  // open: en
  assign bit_extender_1_out = {{12{1'b0}}, rom_1_data[3:0]};  // Bit_Extender bit_extender_1
  _16_Bit_Register u_16_bit_register_1 (
    .WRITEREGISTER(multiplexer_1_out), .WRITEDATA(multiplexer_3_out),
    .READDATA1(n16_bit_register_1_readdata1), .READREGISTER1(rom_1_data_2),
    .READDATA2(n16_bit_register_1_readdata2), .READREGISTER2(rom_1_data[7:4]), .WRITECONTROL(clock_1_out),
    .CONTROL(in_2));
  Bit_Extender #(.in_width(4), .out_width(2)) bit_extender_2 (.in(rom_1_data[15:12]), .out(bit_extender_2_out));
  _16_Bit_ALU u_16_bit_alu_1 (
    .CIN(in_1), .A(n16_bit_register_1_readdata1), .B(multiplexer_2_out), .S(bit_extender_2_out),
    .SUM(n16_bit_alu_1_sum), .ZEROFLAG(out_10), .OVERFLOW(out_11), .COUT(out_12));
  Multiplexer #(.width(16)) multiplexer_2 (
    .in0(n16_bit_register_1_readdata2), .in1(bit_extender_1_out), .out(multiplexer_2_out), .sel(in_7));  // open: en
  RAM #(.addrWidth(16), .dataWidth(16), .bus("separate")) ram_1 (
    .addr(n16_bit_alu_1_sum), .din(n16_bit_register_1_readdata2), .data(ram_1_data), .str(in_3), .sel(in_5),
    .clk(clock_1_out), .ld(in_6));  // open: clr
  Multiplexer #(.width(16)) multiplexer_3 (
    .in0(n16_bit_alu_1_sum), .in1(ram_1_data), .out(multiplexer_3_out), .sel(in_8));  // open: en
endmodule
